// Logisim project 851769-BR32test.circ as structural Verilog: 3 circuits, main circuit BR4
module BR4 (
  input  clk,
  input  reset,
  input  [31:0] BusW,
  input  RegWr,
  input  [1:0] RW,
  input  [1:0] RA,
  input  [1:0] RB,
  output [31:0] Bus_A,
  output [31:0] Bus_B
);

  wire decoder_1_out0, decoder_1_out1, decoder_1_out2, decoder_1_out3;
  wire [31:0] register_1_q, register_2_q, register_3_q, register_4_q;

  Decoder #(.select(2), .disabled(0)) decoder_1 (
    .out0(decoder_1_out0), .out1(decoder_1_out1), .out2(decoder_1_out2), .out3(decoder_1_out3), .sel(RW),
    .en(RegWr));
  Register #(.width(32)) register_1 (.D(BusW), .en(decoder_1_out0), .Q(register_1_q), .clk(clk), .clr(reset));
  Register #(.width(32)) register_2 (.D(BusW), .en(decoder_1_out1), .Q(register_2_q), .clk(clk), .clr(reset));
  Register #(.width(32)) register_3 (.D(BusW), .en(decoder_1_out2), .Q(register_3_q), .clk(clk), .clr(reset));
  Register #(.width(32)) register_4 (.D(BusW), .en(decoder_1_out3), .Q(register_4_q), .clk(clk), .clr(reset));
  Multiplexer #(.select(2), .width(32), .enable("false")) multiplexer_1 (
    .in0(register_1_q), .in1(register_2_q), .in2(register_3_q), .in3(register_4_q), .out(Bus_A), .sel(RA));
  Multiplexer #(.select(2), .width(32), .enable("false")) multiplexer_2 (
    .in0(register_1_q), .in1(register_2_q), .in2(register_3_q), .in3(register_4_q), .out(Bus_B), .sel(RB));
endmodule

module BR32 (
  input  [4:0] RA,
  input  clk,
  input  [4:0] RW,
  input  [31:0] BusW,
  input  reset,
  input  [4:0] RB,
  input  RegWr,
  output [31:0] BusA,
  output [31:0] BusB
);

  wire decoder_1_out0, decoder_1_out1, decoder_1_out2, decoder_1_out3, decoder_1_out4, decoder_1_out5,
       decoder_1_out6, decoder_1_out7;
  wire [31:0] br4_1_bus_a, br4_1_bus_b, br4_2_bus_a, br4_2_bus_b, br4_3_bus_a, br4_3_bus_b, br4_4_bus_a,
       br4_4_bus_b, br4_5_bus_a, br4_5_bus_b, br4_6_bus_a, br4_6_bus_b, br4_7_bus_a, br4_7_bus_b,
       br4_8_bus_a, br4_8_bus_b;

  Decoder #(.select(3), .disabled(0)) decoder_1 (
    .out0(decoder_1_out0), .out1(decoder_1_out1), .out2(decoder_1_out2), .out3(decoder_1_out3),
    .out4(decoder_1_out4), .out5(decoder_1_out5), .out6(decoder_1_out6), .out7(decoder_1_out7),
    .sel(RW[4:2]), .en(RegWr));
  BR4 br4_1 (
    .clk(clk), .reset(reset), .BusW(BusW), .RegWr(decoder_1_out0), .RW(RW[1:0]), .RA(RA[1:0]), .RB(RB[1:0]),
    .Bus_A(br4_1_bus_a), .Bus_B(br4_1_bus_b));
  BR4 br4_2 (
    .clk(clk), .reset(reset), .BusW(BusW), .RegWr(decoder_1_out1), .RW(RW[1:0]), .RA(RA[1:0]), .RB(RB[1:0]),
    .Bus_A(br4_2_bus_a), .Bus_B(br4_2_bus_b));
  BR4 br4_3 (
    .clk(clk), .reset(reset), .BusW(BusW), .RegWr(decoder_1_out2), .RW(RW[1:0]), .RA(RA[1:0]), .RB(RB[1:0]),
    .Bus_A(br4_3_bus_a), .Bus_B(br4_3_bus_b));
  BR4 br4_4 (
    .clk(clk), .reset(reset), .BusW(BusW), .RegWr(decoder_1_out3), .RW(RW[1:0]), .RA(RA[1:0]), .RB(RB[1:0]),
    .Bus_A(br4_4_bus_a), .Bus_B(br4_4_bus_b));
  BR4 br4_5 (
    .clk(clk), .reset(reset), .BusW(BusW), .RegWr(decoder_1_out4), .RW(RW[1:0]), .RA(RA[1:0]), .RB(RB[1:0]),
    .Bus_A(br4_5_bus_a), .Bus_B(br4_5_bus_b));
  BR4 br4_6 (
    .clk(clk), .reset(reset), .BusW(BusW), .RegWr(decoder_1_out5), .RW(RW[1:0]), .RA(RA[1:0]), .RB(RB[1:0]),
    .Bus_A(br4_6_bus_a), .Bus_B(br4_6_bus_b));
  BR4 br4_7 (
    .clk(clk), .reset(reset), .BusW(BusW), .RegWr(decoder_1_out6), .RW(RW[1:0]), .RA(RA[1:0]), .RB(RB[1:0]),
    .Bus_A(br4_7_bus_a), .Bus_B(br4_7_bus_b));
  BR4 br4_8 (
    .clk(clk), .reset(reset), .BusW(BusW), .RegWr(decoder_1_out7), .RW(RW[1:0]), .RA(RA[1:0]), .RB(RB[1:0]),
    .Bus_A(br4_8_bus_a), .Bus_B(br4_8_bus_b));
  Multiplexer #(.select(3), .width(32), .disabled(0), .enable("false")) multiplexer_1 (
    .in0(br4_1_bus_a), .in1(br4_2_bus_a), .in2(br4_3_bus_a), .in3(br4_4_bus_a), .in4(br4_5_bus_a),
    .in5(br4_6_bus_a), .in6(br4_7_bus_a), .in7(br4_8_bus_a), .out(BusA), .sel(RA[4:2]));
  Multiplexer #(.select(3), .width(32), .disabled(0), .enable("false")) multiplexer_2 (
    .in0(br4_1_bus_b), .in1(br4_2_bus_b), .in2(br4_3_bus_b), .in3(br4_4_bus_b), .in4(br4_5_bus_b),
    .in5(br4_6_bus_b), .in6(br4_7_bus_b), .in7(br4_8_bus_b), .out(BusB), .sel(RB[4:2]));

  // Other names for the same wires on the sheet: RA_t[1:0] = RA[1:0]; RA_32[2:0] = RA[4:2]; RB_t[1:0] = RB[1:0];
  //   RB_32[2:0] = RB[4:2]; RW_t[1:0] = RW[1:0]; RW_32[2:0] = RW[4:2]
endmodule

module main (
);

  wire br32test_1_p5, br32test_1_p7, br32test_1_p9, br32test_1_p11, clk_out, reset_out;
  wire [4:0] br32test_1_p1, br32test_1_p3, br32test_1_p10;
  wire [31:0] br32_1_busa, br32_1_busb, br32test_1_p12;

  Clock clk (.out(clk_out));
  Button reset (.out(reset_out));
  BR32 br32_1 (
    .RA(br32test_1_p1), .clk(clk_out), .RW(br32test_1_p10), .BusW(br32test_1_p12), .reset(reset_out),
    .RB(br32test_1_p3), .RegWr(br32test_1_p11), .BusA(br32_1_busa), .BusB(br32_1_busb));
  // Probe on br32test_1_p7
  // Probe on br32test_1_p5
  // BR32test br32test_1: pin names not known; wires that end beside it: br32test_1_p1, br32_1_busa, br32test_1_p3, br32_1_busb, br32test_1_p5, clk_out, br32test_1_p7, reset_out, br32test_1_p9, br32test_1_p10, br32test_1_p11, br32test_1_p12
  // Probe on br32test_1_p9
endmodule
